# Fritzing sketch Prototype (saved by Fritzing 0.9.3b)
breadboards: 1

parts:
  Part1 = 16-Channel 12-bit PWM Servo Driver - I2C [part_number=815]
  J1 = Dagu DGServo 9g header connector (female) [package=THT]
  J2 = Dagu DGServo 9g header connector (female) [package=THT]
  J3 = Dagu DGServo 9g header connector (female) [package=THT]
  J4 = Dagu DGServo 9g header connector (female) [package=THT]
  J5 = Dagu DGServo 9g header connector (female) [package=THT]
  J6 = Dagu DGServo 9g header connector (female) [package=THT]
  Part2 = Arduino Uno (Rev3)
  U2 = Voltage Regulator [package=v-reg_dpack]
  J7 = Power Jack [package=power_jack_slot]
  C1 = Capacitor Polarized [package=cpol-radial-10uf-25v]

nets:
  VCC: Part1.5.0V, J1.Vcc, J2.Vcc, J3.Vcc, J4.Vcc, J5.Vcc, J6.Vcc, U2.OUT, C1.+
  GND: Part1.GND, J1.gnd, J2.gnd, J3.gnd, J4.gnd, J5.gnd, J6.gnd, Part2.GND, U2.ADJ, J7.GNDBREAK, C1.-
  N1: Part1.PWM5, J6.pulse
  N2: Part1.PWM4, J5.pulse
  N3: Part1.PWM3, J4.pulse
  N4: Part1.PWM2, J3.pulse
  N5: Part1.PWM1, J2.pulse
  N6: Part1.PWM0, J1.pulse
  N7: Part1.SDA, Part2.A4/SDA
  N8: Part1.SCL, Part2.A5/SCL
  VCC_2: Part1.VCC, Part2.5V
  VIN: Part2.VIN, U2.IN, J7.GND

custom parts:
  16-Channel 12-bit PWM Servo Driver - I2C: You want to make a cool robot, maybe a hexapod walker, or maybe just a piece of art with a lot of moving parts. Or maybe you want to drive a lot of LEDs with precise PWM output. Using only two pins, control 16 free-running PWM outputs! You can even chain up 62 breakouts to control up to 992 PWM outputs.
