# Fritzing sketch Prototype - motor (saved by Fritzing 0.9.3b)

parts:
  Part1 = 16-Channel 12-bit PWM Servo Driver - I2C [part_number=815]
  J1 = Dagu DGServo 9g header connector (female) [package=THT]
  J2 = Dagu DGServo 9g header connector (female) [package=THT]
  J3 = Dagu DGServo 9g header connector (female) [package=THT]
  J4 = Dagu DGServo 9g header connector (female) [package=THT]
  J5 = Dagu DGServo 9g header connector (female) [package=THT]
  J6 = Dagu DGServo 9g header connector (female) [package=THT]
  U2 = Voltage Regulator [package=v-reg_dpack]
  J7 = Power Jack [package=power_jack_slot]
  C1 = Capacitor Polarized [package=cpol-radial-10uf-25v]
  Part3 = Arduino Nano (Rev3.0) (ICSP)
  Part4 = Motor Driver 1A Dual TB6612FNG
  JP1 = Header 2 [package=molex-1x2_lock]
  JP2 = Header 2 [package=molex-1x2_lock]
  Raspberry_Pi1 = Raspberry Pi 2  # not connected

nets:
  VCC: Part1.5.0V, J1.Vcc, J2.Vcc, J3.Vcc, J4.Vcc, J5.Vcc, J6.Vcc, U2.OUT, C1.+
  GND: Part1.GND, J1.gnd, J2.gnd, J3.gnd, J4.gnd, J5.gnd, J6.gnd, U2.ADJ, J7.GNDBREAK, C1.-, Part3.GND, Part4.GND
  N1: Part1.PWM5, J6.pulse
  N2: Part1.PWM4, J5.pulse
  N3: Part1.PWM3, J4.pulse
  N4: Part1.PWM2, J3.pulse
  N5: Part1.PWM1, J2.pulse
  N6: Part1.PWM0, J1.pulse
  N7: Part1.SDA, Part3.A4
  VCC_2: Part1.VCC, Part3.5V, Part4.VCC
  N8: Part1.SCL, Part3.A5
  GND_2: U2.IN, J7.GND, Part3.VIN, Part4.VM
  N9: Part3.D2, Part4.PWMB
  N10: Part3.D3, Part4.BIN2
  N11: Part3.D4, Part4.BIN1
  N12: Part3.D5, Part4.STBY
  N13: Part3.D6, Part4.AIN1
  N14: Part3.D7, Part4.AIN2
  N15: Part3.D8, Part4.PWMA
  N16: Part4.B01, JP2.1
  N17: Part4.B02, JP2.2
  N18: Part4.A02, JP1.1
  N19: Part4.A01, JP1.2

notes:
  To Arduino
  to Raspberry Pi
  WiFi dongle + webcam

custom parts:
  16-Channel 12-bit PWM Servo Driver - I2C: You want to make a cool robot, maybe a hexapod walker, or maybe just a piece of art with a lot of moving parts. Or maybe you want to drive a lot of LEDs with precise PWM output. Using only two pins, control 16 free-running PWM outputs! You can even chain up 62 breakouts to control up to 992 PWM outputs.
